# Fritzing sketch Fritzing Sketches (saved by Fritzing 0.9.3b)
breadboards: 3

parts:
  Part1 = Arduino Uno (Rev3)
  Raspberry_Pi_1 = Raspberry Pi 3 [part_number=RPI-3-V1.2]  # not connected
  LCD2 = LCD screen
  LCM1602_IIC2 = LCM1602 IIC [part_number="LCM1602 IIC" chip_label="LCM1602 IIC" package="DIP (Dual Inline) [THT]"]
  4_Channel_Relay2 = 4 Channel Power Relay
  S1 = PH meter [package=THT]
  YwRobot_Power_Supply1 = YwRobot Breadboard Power Supply [part_number=545043]
  M1 = DC Motor
  M2 = DC Motor
  M3 = DC Motor
  R2 = Photocell (LDR) [package=THT]
  R3 = Resistor [tolerance=±5% resistance=220 package="0603 [SMD]"]
  R4 = Resistor [tolerance=±5% resistance=220 package="0603 [SMD]"]
  LED1 = smd LED [color="Red (633nm)" package="0805 [SMD]"]
  LED2 = LEDs [package=led10mm]
  Power_plug1 = Power plug
  CONN1 = USB connector [package=THT]
  CONN2 = USB connector [package=THT]

nets:
  N1: Part1.A0, S1.pin1
  N2: Part1.A1, R2.pin_0, R3.Pin_1
  N3: Part1.A4/SDA, LCM1602_IIC2.SDA
  N4: Part1.A5/SCL, LCM1602_IIC2.SCL
  N5: Part1.D13/SCK, R4.Pin_0
  N6: Part1.D2, 4_Channel_Relay2.IN1
  N7: Part1.D3_PWM, 4_Channel_Relay2.IN2
  N8: Part1.D4, 4_Channel_Relay2.IN3
  N9: Part1.D5_PWM, 4_Channel_Relay2.IN4
  5V: Part1.5V, LCM1602_IIC2.VCC, S1.pin2, R2.pin_1
  GND: Part1.GND, LCM1602_IIC2.GND, S1.pin3, R3.Pin_0, LED1.anode
  VSS: LCD2.VSS, LCM1602_IIC2.VSS
  VDD: LCD2.VDD, LCM1602_IIC2.VDD
  N10: LCD2.V0, LCM1602_IIC2.V0
  N11: LCD2.RS, LCM1602_IIC2.RS
  N12: LCD2.R/W, LCM1602_IIC2.RW
  N13: LCD2.E, LCM1602_IIC2.E
  N14: LCD2.DB0, LCM1602_IIC2.D0
  N15: LCD2.DB1, LCM1602_IIC2.D1
  N16: LCD2.DB2, LCM1602_IIC2.D2
  N17: LCD2.DB3, LCM1602_IIC2.D3
  N18: LCD2.DB4, LCM1602_IIC2.D4
  N19: LCD2.DB5, LCM1602_IIC2.D5
  N20: LCD2.DB6, LCM1602_IIC2.D6
  N21: LCD2.DB7, LCM1602_IIC2.D7
  N22: LCD2.LED+, LCM1602_IIC2.A
  N23: LCD2.LED-, LCM1602_IIC2.K
  N24: LCM1602_IIC2.LED_A, LCM1602_IIC2.LED_B
  N25: 4_Channel_Relay2.GND, YwRobot_Power_Supply1.GND#13
  N26: 4_Channel_Relay2.VCC, 4_Channel_Relay2.COM#20, 4_Channel_Relay2.COM#23, 4_Channel_Relay2.COM#26, YwRobot_Power_Supply1.VCC#9
  N27: 4_Channel_Relay2.COM#17, Power_plug1.VCC
  N28: 4_Channel_Relay2.NO, LED2.A
  N29: YwRobot_Power_Supply1.GND#11, M1.pin_2, M2.pin_2, M3.pin_2
  N30: LED2.C, Power_plug1.GND
  5V_2: CONN1.5V, CONN2.5V
  N31: CONN1.d-, CONN2.d-
  N32: CONN1.d+, CONN2.d+
  GND_2: CONN1.GND, CONN1.chassis5, CONN1.chassis6, CONN2.GND, CONN2.chassis5

notes:
  Arduino to RPi USB
  PH & EC SENSOR
  16x2 LCD
  PUMP1
  PUMP2
  PUMP3
  Arduino Uno
  Breadboard 5V Power Supply
  Raspberry Pi 3B+
  Light Source
  Light Sensor

custom parts:
  LCM1602 IIC: I2C-Module to use a 1602 or 2004 LCD on with the wire.h libory Serial LCD Modul
  4 Channel Power Relay: A 4 channel power relay. The module operates at 5V.
  YwRobot Breadboard Power Supply: The YwRobot Breadboard Power Supply (MB-V2) has two power rails; they can be 5V or 3V3. Power to the module can be provided through the female USB socket or through the A10 (female) 2.1mm power jack.
  LEDs: LEDs Standard schematic elements and footprints for 5mm, 3mm, 1206, and 0603 sized LEDs. 5mm - Spark Fun Electronics SKU : COM-00529 (and others)
